// Logisim project RV32I-modded-logisim.circ as structural Verilog: 9 circuits, main circuit main
module main (
  input  in_1
);

  wire and_1_out, and_3_out, AUIPC, branch_evaluator_1_out_4, clock_1_out, comparator_1_eq, comparator_2_eq,
       comparator_3_eq, comparator_4_eq, comparator_5_eq, JAL, JALR, ld, LUI, not_1_out, not_2_out,
       not_3_out, not_4_out, not_5_out, not_6_out, not_7_out, not_8_out, not_9_out, not_10_out, not_11_out,
       not_12_out, not_13_out, not_14_out, or_1_out, or_2_out, register_write_1_out_2, st;
  wire [2:0] funct3;
  wire [4:0] immediate_decoder_1_rd, immediate_decoder_1_rs1, immediate_decoder_1_rs2, multiplexer_1_out,
       multiplexer_2_out;
  wire [6:0] funct7, opcode;
  wire [11:0] immediate_decoder_1_i, immediate_decoder_1_s;
  wire [12:0] immediate_decoder_1_b;
  wire [19:0] immediate_decoder_1_u;
  wire [23:0] counter_1_q, transistor_1_out_2;
  wire [31:0] adder_1_out, adder_2_out, adder_3_out, adder_4_out, adder_5_out, adder_6_out, alu_1_out_6,
       bit_extender_1_out, data_in_stapler_1_combined_data, data_out_slicer_1_out_4, Ii32b,
       immediate_decoder_1_j, multiplexer_3_out, multiplexer_4_out, multiplexer_5_out, multiplexer_6_out,
       multiplexer_7_out, multiplexer_8_out, multiplexer_9_out, ram_1_data, ram_2_data, ram_3_data,
       register_1_q, register_2_q, rom_1_data, Si32b, transistor_1_out, transistor_5_out;

  Clock clock_1 (.out(clock_1_out));
  LUI_AUIPC_JAL_JALR lui_auipc_jal_jalr_1 (
    .in_1(opcode), .JALR(JALR), .JAL(JAL), .AUIPC(AUIPC), .LUI(LUI), .Load(ld), .Store(st));
  and and_1 (and_1_out, clock_1_out, not_2_out);
  not not_1 (not_1_out, clock_1_out);
  not not_2 (not_2_out, not_1_out);
  Transistor #(.\type ("n"), .gate("br"), .width(32)) transistor_1 (
    .in(32'h101e0), .out({transistor_1_out[31:26], transistor_1_out_2, transistor_1_out[1:0]}), .gate(in_1));
  Transistor #(.\type ("n"), .gate("br"), .width(32)) transistor_2 (
    .in(adder_5_out), .out({transistor_1_out[31:26], transistor_1_out_2, transistor_1_out[1:0]}), .gate(JALR));
  Counter #(.width(24), .max('hffffff), .trigger("falling")) counter_1 (
    .load(or_1_out), .D(transistor_1_out_2), .count(not_3_out), .Q(counter_1_q), .clk(and_1_out));  // open: carry, clr
  not not_3 (not_3_out, or_1_out);
  or or_1 (or_1_out, in_1, JAL, and_3_out, JALR);
  Transistor #(.\type ("n"), .gate("br"), .width(32)) transistor_3 (
    .in(adder_2_out), .out({transistor_1_out[31:26], transistor_1_out_2, transistor_1_out[1:0]}), .gate(JAL));
  not not_4 (not_4_out, clock_1_out);
  not not_5 (not_5_out, not_6_out);
  not not_6 (not_6_out, not_4_out);
  Transistor #(.\type ("n"), .gate("br"), .width(32)) transistor_4 (
    .in(adder_1_out), .out({transistor_1_out[31:26], transistor_1_out_2, transistor_1_out[1:0]}),
    .gate(and_3_out));
  not not_7 (not_7_out, not_8_out);
  not not_8 (not_8_out, not_9_out);
  not not_9 (not_9_out, not_5_out);
  ROM #(.addrWidth(24), .dataWidth(32)) rom_1 (.addr(counter_1_q), .data(rom_1_data));  // open: sel
  assign bit_extender_1_out = {{19{immediate_decoder_1_b[12]}}, immediate_decoder_1_b};  // Bit_Extender bit_extender_1
  Adder #(.width(32)) adder_1 (
    .a(bit_extender_1_out), .b({{6{1'b0}}, counter_1_q, 2'b00}), .out(adder_1_out));  // open: cin, cout
  Adder #(.width(32)) adder_2 (
    .a(immediate_decoder_1_j), .b({{6{1'b0}}, counter_1_q, 2'b00}), .out(adder_2_out));  // open: cin, cout
  not not_10 (not_10_out, not_7_out);
  immediate_decoder immediate_decoder_1 (
    .in_1(rom_1_data), .rd(immediate_decoder_1_rd), .rs1(immediate_decoder_1_rs1),
    .rs2(immediate_decoder_1_rs2), .funct3(funct3), .funct7(funct7), .I(immediate_decoder_1_i),
    .S(immediate_decoder_1_s), .B(immediate_decoder_1_b), .U(immediate_decoder_1_u),
    .J(immediate_decoder_1_j), .opcode(opcode));
  assign Ii32b = {{20{immediate_decoder_1_i[11]}}, immediate_decoder_1_i};  // Bit_Extender bit_extender_2
  assign Si32b = {{20{1'b0}}, immediate_decoder_1_s};  // Bit_Extender bit_extender_3
  Adder #(.width(32)) adder_3 (
    .a({immediate_decoder_1_u, {12{1'b0}}}), .b({{6{1'b0}}, counter_1_q, 2'b00}), .out(adder_3_out));  // open: cin, cout
  Adder #(.width(32)) adder_4 (.a({{6{1'b0}}, counter_1_q, 2'b00}), .b(32'h4), .out(adder_4_out));  // open: cin, cout
  Adder #(.width(32)) adder_5 (.a(register_1_q), .b(Ii32b), .out(adder_5_out));  // open: cin, cout
  not not_11 (not_11_out, and_1_out);
  not not_12 (not_12_out, not_11_out);
  not not_13 (not_13_out, not_12_out);
  not not_14 (not_14_out, not_13_out);
  Multiplexer #(.width(5)) multiplexer_1 (
    .in0(immediate_decoder_1_rs1), .in1(immediate_decoder_1_rd), .out(multiplexer_1_out), .sel(and_1_out));  // open: en
  Multiplexer #(.width(5)) multiplexer_2 (
    .in0(immediate_decoder_1_rs2), .in1(immediate_decoder_1_rd), .out(multiplexer_2_out), .sel(and_1_out));  // open: en
  Multiplexer #(.width(32)) multiplexer_3 (
    .in0(multiplexer_4_out), .in1({immediate_decoder_1_u, {12{1'b0}}}), .out(multiplexer_3_out), .sel(LUI));  // open: en
  Multiplexer #(.width(32)) multiplexer_4 (
    .in0(multiplexer_5_out), .in1(adder_3_out), .out(multiplexer_4_out), .sel(AUIPC));  // open: en
  or or_2 (or_2_out, JALR, JAL);
  Multiplexer #(.width(32)) multiplexer_5 (
    .in0(multiplexer_9_out), .in1(adder_4_out), .out(multiplexer_5_out), .sel(or_2_out));  // open: en
  register_write register_write_1 (.in_1(opcode), .out_2(register_write_1_out_2));
  Comparator #(.width(5), .mode("unsigned")) comparator_1 (
    .a({5{1'b0}}), .b(multiplexer_1_out), .eq(comparator_1_eq));  // open: gt, lt
  Comparator #(.width(5), .mode("unsigned")) comparator_2 (
    .a({5{1'b0}}), .b(multiplexer_2_out), .eq(comparator_2_eq));  // open: gt, lt
  RAM #(.addrWidth(5), .dataWidth(32), .bus("separate")) ram_1 (
    .addr(multiplexer_1_out), .din(multiplexer_3_out), .data(ram_1_data), .str(register_write_1_out_2),
    .clk(not_14_out), .ld(1'b1));  // open: sel, clr
  RAM #(.addrWidth(5), .dataWidth(32), .bus("separate")) ram_2 (
    .addr(multiplexer_2_out), .din(multiplexer_3_out), .data(ram_2_data), .str(register_write_1_out_2),
    .clk(not_14_out), .ld(1'b1));  // open: sel, clr
  Comparator #(.width(7), .mode("unsigned")) comparator_3 (
    .a(7'b1110011), .b(opcode), .eq(comparator_3_eq));  // open: gt, lt
  Transistor #(.\type ("n"), .width(32)) transistor_5 (.in(Ii32b), .out(transistor_5_out), .gate(ld));
  Transistor #(.\type ("n"), .width(32)) transistor_6 (.in(Si32b), .out(transistor_5_out), .gate(st));
  Pull_Resistor pull_resistor_1 (.node(transistor_5_out));
  Register #(.width(32), .trigger("high")) register_1 (
    .D(multiplexer_6_out), .Q(register_1_q), .clk(not_10_out));  // open: en, clr
  Multiplexer #(.width(32)) multiplexer_6 (
    .in0(ram_1_data), .in1({32{1'b0}}), .out(multiplexer_6_out), .sel(comparator_1_eq));  // open: en
  Register #(.width(32), .trigger("high")) register_2 (
    .D(multiplexer_7_out), .Q(register_2_q), .clk(not_10_out));  // open: en, clr
  Multiplexer #(.width(32)) multiplexer_7 (
    .in0(ram_2_data), .in1({32{1'b0}}), .out(multiplexer_7_out), .sel(comparator_2_eq));  // open: en
  // ECall #(.trigger("falling")) ecall_1: pin names not known
  // AND_Gate and_2 has open pins: in0=not_10_out, in1=comparator_3_eq, out=open
  Adder #(.width(32)) adder_6 (.a(transistor_5_out), .b(register_1_q), .out(adder_6_out));  // open: cin, cout
  data_in_stapler data_in_stapler_1 (
    .address(adder_6_out), .to_write(register_2_q), .current_value_at_location(ram_3_data),
    .combined_data(data_in_stapler_1_combined_data), .funct3(funct3));
  Comparator #(.width(7), .mode("unsigned")) comparator_4 (
    .a(7'b0010011), .b(opcode), .eq(comparator_4_eq));  // open: gt, lt
  branch_evaluator branch_evaluator_1 (
    .rs1(register_1_q), .rs2(register_2_q), .out_4(branch_evaluator_1_out_4), .funct3(funct3));
  Comparator #(.width(7), .mode("unsigned")) comparator_5 (
    .a(7'b1100011), .b(opcode), .eq(comparator_5_eq));  // open: gt, lt
  and and_3 (and_3_out, comparator_5_eq, branch_evaluator_1_out_4);
  Multiplexer #(.width(32)) multiplexer_8 (
    .in0(register_2_q), .in1(Ii32b), .out(multiplexer_8_out), .sel(comparator_4_eq));  // open: en
  RAM #(.addrWidth(24), .dataWidth(32), .bus("separate")) ram_3 (
    .addr(adder_6_out[23:0]), .din(data_in_stapler_1_combined_data), .data(ram_3_data), .str(st),
    .clk(not_14_out), .ld(1'b1));  // open: sel, clr
  ALU alu_1 (
    .rs1(register_1_q), .rs2(multiplexer_8_out), .immediate(comparator_4_eq), .out_6(alu_1_out_6),
    .funct7_i_think(funct7), .funct3(funct3));
  Multiplexer #(.width(32)) multiplexer_9 (
    .in0(alu_1_out_6), .in1(data_out_slicer_1_out_4), .out(multiplexer_9_out), .sel(ld));  // open: en
  data_out_slicer data_out_slicer_1 (
    .address(adder_6_out), .RAM_data(ram_3_data), .funct3(funct3), .out_4(data_out_slicer_1_out_4));

  // Notes on the sheet:
  //   splitter discards 2 least significant and 6 most significant bits
  //   control state B
  //   control state A
  //   contents of rom_1 (hex, n*v repeats v):
  //   16413*0 fd010113 2812423 2912223 3212023 1312e23 1412c23 1512a23 2112623 1612823 1712623 413 493
  //   200993 300a93 100a13 3e800913 147793 c078663 b47793 c078263 ffc40793 cf9f263 140413 ff2412e3 2800513
  //   7d1000ef 50b13 48513 4dd000ef 247b7 9c07aa03 50a93 b0493 413 229b7 a00913 40513 4b9000ef a0593
  //   d5000ef a8593 478000ef 435000ef 50793 50593 f4a023 2098513 140413 6f4010ef 448493 fd2414e3 225b7
  //   900613 2458593 100513 76c010ef 2c12083 2812403 b0513 2412483 2012903 1c12983 1812a03 1412a83 1012b03
  //   c12b83 3010113 8067 8484b3 f3dff06f 347793 f3578ee3 40b93 b13 fffb8513 1c8000ef ffeb8b93 ab0b33
  //   ff7a48e3 ffcb0793 100713 fff78b13 78593 70513 fa5a63 51d000ef 50713 b0793 fe5ff06f e484b3 ef1ff06f
  //   14197 fc818193 83018513 88c18613 40a60633 593 50c010ef 1517 d9c50513 551000ef 601000ef 12503 410593
  //   613 e5dff0ef 54d0006f 8067 24537 247b7 9a450713 9a478793 e78c63 337 30313 30663 9a450513 30067 8067
  //   247b7 24537 9a478593 9a450793 40f585b3 4025d593 1f5d793 b785b3 4015d593 58c63 337 30313 30663
  //   9a450513 30067 8067 8441c703 4071663 ff010113 812423 112623 78413 f7dff0ef 7b7 78793 78a63 23537
  //   d4450513 ffff0097 d40080e7 100793 84f18223 c12083 812403 1010113 8067 8067 7b7 78793 2078463 23537
  //   ff010113 84818593 d4450513 112623 ffff0097 cfc080e7 c12083 1010113 f3dff06f 100793 4a7d263 ff010113
  //   912223 50593 112623 812423 100513 100493 fff58413 3a5000ef 40593 fe941ae3 c12083 812403 412483
  //   1010113 8067 100513 8067 fa010113 4112e23 4812c23 4912a23 5212823 5312623 5412423 5512223 5612023
  //   3712e23 3812c23 3912a23 3a12823 3b12623 100793 12623 1ea7d063 100d93 200793 1cf50463 ffe50793 f12e23
  //   f12a23 12823 200a93 78713 70793 11b70a63 12423 13578a63 ffe78793 f12c23 f12023 12223 78b93 9b78c63
  //   c13 d5b8263 ffeb8b93 b8993 b13 98913 5b98e63 a13 9590e63 ffe90913 90413 493 40d13 3b40063 c93
  //   fffd0513 f31ff0ef ffed0d13 ac8cb3 ffadc8e3 1c8d13 fff40713 1a484b3 ffe40413 fcedc8e3 148493 9a0a33
  //   fb2dcae3 1a0913 fff98793 12b0b33 ffe98993 f8fdcae3 1b0b13 16c0c33 f77dcce3 1c0b93 412683 12703
  //   17686b3 fff70793 d12223 ffe70c93 2fdd463 1912023 c8793 f41ff06f 100493 ffea8913 fa5ff06f 100b13
  //   ffea8b93 fb9ff06f 1812783 168d13 812703 1a70733 e12423 eefdcee3 170793 1012603 1412683 f607b3 f12823
  //   fff68713 ffe68793 2edd063 f12a23 78713 ec5ff06f ffea8793 100d13 f12c23 fb9ff06f 1012783 178793
  //   c12703 1c12503 f707b3 f12623 e6adcce3 5c12083 5812403 5412483 5012903 4c12983 4812a03 4412a83
  //   4012b03 3c12b83 3812c03 3412c83 3012d03 2c12d83 178513 6010113 8067 100793 12e23 fa5ff06f c12783
  //   fb1ff06f 8007b7 ff010113 fff78793 a7f733 812423 1212023 1755413 1f55913 175d513 b7f7b3 ff47413
  //   ff57513 112623 912223 1f5d593 371613 379793 40a40733 18b91e63 ae05863 6051863 79c63 ff00793 4f40c63
  //   60793 40513 bc0006f fff70713 2071e63 c787b3 40513 579713 a075263 150513 ff00713 32e50463 7e000737
  //   17f693 fff70713 17d793 e7f7b3 d7e7b3 7c0006f ff00693 2d41063 60793 ff00513 680006f ff00693 fed408e3
  //   40006b7 d7e7b3 1b00693 e6d663 100793 f99ff06f 2000693 40e686b3 e7d5b3 d797b3 f037b3 f5e7b3 f7dff06f
  //   8070463 4041063 2060063 fff00693 d71663 c787b3 f69ff06f ff00693 fff74713 2d51a63 77f713 28070863
  //   f7f713 400693 28d70263 478793 27c0006f ff00693 fed500e3 40006b7 40e00733 d66633 1b00693 e6d663
  //   100713 1c0006f 2000693 e655b3 40e68733 e61733 e03733 e5e733 e787b3 efdff06f 140513 ff57693 100713
  //   4d74063 2041863 513 f80604e3 20078663 c787b3 579713 f6075ce3 fc000737 fff70713 e7f7b3 100513
  //   f65ff06f ee060ae3 16079463 ee9ff06f ff00713 1ee50063 f60733 175793 f45ff06f 8e05063 4051663 e60786e3
  //   fff70713 2071463 40f607b3 40513 579713 f20750e3 40004b7 fff48493 97f4b3 50413 13c0006f ff00693
  //   e8d40ae3 1b00693 2e6d063 100793 fc9ff06f ff00693 e6d40ee3 40006b7 d7e7b3 fe1ff06f 2000693 e7d5b3
  //   40e68733 e797b3 f037b3 f5e7b3 f99ff06f 6070e63 2041e63 58913 ea060ae3 fff00693 d71863 40c787b3 58913
  //   f7dff06f ff00693 fff74713 e8d50ae3 1b00693 2e6d463 100713 380006f ff00693 58913 e6d50ce3 40006b7
  //   40e00733 d66633 fd9ff06f 2000693 e65833 40e68733 e61733 e03733 e86733 40e787b3 fa5ff06f 140713
  //   ff77713 100693 4e6ca63 2041c63 61863 12079e63 513 380006f 12078c63 40f60733 571693 40c787b3 1206c0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
  //   add 2 bits on the bottom, and 6 on the top
  //   branch evaluator output
  //   rs1 + sign extended I-immediate for JALR instruction
  //   no need to set LSB to zero as bottom 2 bits will be discarded anyway
  //   JAL and JALR both write PC+4 to rd
  //   rs1 line to to add to sign extended I-immediate for JALR instruction
  //   branch is opcode 1100011
endmodule

module immediate_decoder (
  input  [31:0] in_1,
  output [4:0] rd,
  output [4:0] rs1,
  output [6:0] opcode,
  output [4:0] rs2,
  output [2:0] funct3,
  output [6:0] funct7,
  output [11:0] I,
  output [11:0] S,
  output [12:0] B,
  output [19:0] U,
  output [31:0] J
);

  assign J = {{11{in_1[31]}}, {in_1[31], in_1[19:12], in_1[20], in_1[30:21], 1'b0}};  // Bit_Extender bit_extender_1

  assign B = {in_1[31], in_1[7], in_1[30:25], in_1[11:8], 1'b0};
  assign funct3 = in_1[14:12];
  assign funct7 = in_1[31:25];
  assign I = in_1[31:20];
  assign opcode = in_1[6:0];
  assign rd = in_1[11:7];
  assign rs1 = in_1[19:15];
  assign rs2 = in_1[24:20];
  assign S = {in_1[31:25], in_1[11:7]};
  assign U = in_1[31:12];
endmodule

module ALU (
  input  [6:0] funct7_i_think,
  input  [31:0] rs1,
  input  [31:0] rs2,
  input  immediate,
  input  [2:0] funct3,
  output [31:0] out_6
);

  wire and_1_out, comparator_1_gt, comparator_2_gt, not_1_out;
  wire [31:0] adder_1_out, and_2_out, bit_extender_1_out, bit_extender_2_out, multiplexer_1_out,
       multiplexer_2_out, or_1_out, shifter_1_out, shifter_2_out, shifter_3_out, subtractor_1_out, xor_1_out;

  not not_1 (not_1_out, immediate);
  Adder #(.width(32)) adder_1 (.a(rs1), .b(rs2), .out(adder_1_out));  // open: cin, cout
  Subtractor #(.width(32)) subtractor_1 (.a(rs1), .b(rs2), .out(subtractor_1_out));  // open: bin, bout
  Shifter #(.width(32)) shifter_1 (.in(rs1), .\dist (rs2[4:0]), .out(shifter_1_out));
  Comparator #(.width(32)) comparator_1 (.a(rs1), .b(rs2), .gt(comparator_1_gt));  // open: eq, lt
  Comparator #(.width(32), .mode("unsigned")) comparator_2 (.a(rs1), .b(rs2), .gt(comparator_2_gt));  // open: eq, lt
  Shifter #(.width(32), .shift("lr")) shifter_2 (.in(rs1), .\dist (rs2[4:0]), .out(shifter_2_out));
  Shifter #(.width(32), .shift("ar")) shifter_3 (.in(rs1), .\dist (rs2[4:0]), .out(shifter_3_out));
  Multiplexer #(.width(32)) multiplexer_1 (
    .in0(adder_1_out), .in1(subtractor_1_out), .out(multiplexer_1_out), .sel(and_1_out));  // open: en
  and and_1 (and_1_out, not_1_out, funct7_i_think[5]);
  assign xor_1_out = rs1 ^ rs2;  // XOR_Gate xor_1, 32 bits wide
  Multiplexer #(.width(32)) multiplexer_2 (
    .in0(shifter_2_out), .in1(shifter_3_out), .out(multiplexer_2_out), .sel(funct7_i_think[5]));  // open: en
  assign or_1_out = rs1 | rs2;  // OR_Gate or_1, 32 bits wide
  assign and_2_out = rs1 & rs2;  // AND_Gate and_2, 32 bits wide
  assign bit_extender_1_out = {{31{1'b0}}, comparator_1_gt};  // Bit_Extender bit_extender_1
  assign bit_extender_2_out = {{31{1'b0}}, comparator_2_gt};  // Bit_Extender bit_extender_2
  Multiplexer #(.select(3), .width(32)) multiplexer_3 (
    .in0(multiplexer_1_out), .in1(shifter_1_out), .in2(bit_extender_1_out), .in3(bit_extender_2_out),
    .in4(xor_1_out), .in5(multiplexer_2_out), .in6(or_1_out), .in7(and_2_out), .out(out_6), .sel(funct3));  // open: en

  // Notes on the sheet:
  //   ADD
  //   SUB
  //   SLL
  //   SLT
  //   SLTU
  //   XOR
  //   SRL
  //   SRA
  //   OR
  //   AND
  //   bit 5 of funct7 is used a lot
  //   on if rs1 < rs2
endmodule

module immediate_chooser (
  input  [6:0] opcode,
  input  [2:0] funct3,
  output I,
  output R,
  output S,
  output B,
  output U,
  output J
);

  wire comparator_1_eq, comparator_2_eq, comparator_3_eq, comparator_4_eq, comparator_5_eq, comparator_6_eq,
       comparator_9_eq, comparator_10_eq, demultiplexer_1_out0, demultiplexer_1_out1, or_1_out;

  Comparator #(.width(3)) comparator_1 (.a(funct3), .b(3'b001), .eq(comparator_1_eq));  // open: gt, lt
  Comparator #(.width(3)) comparator_2 (.a(funct3), .b(3'b101), .eq(comparator_2_eq));  // open: gt, lt
  or or_1 (or_1_out, comparator_1_eq, comparator_2_eq);
  Comparator #(.width(5)) comparator_3 (.a(opcode[6:2]), .b({5{1'b0}}), .eq(comparator_3_eq));  // open: gt, lt
  Comparator #(.width(5)) comparator_4 (.a(opcode[6:2]), .b(5'b00100), .eq(comparator_4_eq));  // open: gt, lt
  Demultiplexer demultiplexer_1 (
    .out0(demultiplexer_1_out0), .out1(demultiplexer_1_out1), .in(comparator_4_eq), .sel(or_1_out));  // open: en
  Comparator #(.width(5)) comparator_5 (.a(opcode[6:2]), .b(5'b11001), .eq(comparator_5_eq));  // open: gt, lt
  Comparator #(.width(5)) comparator_6 (.a(opcode[6:2]), .b(5'b01100), .eq(comparator_6_eq));  // open: gt, lt
  Comparator #(.width(5)) comparator_7 (.a(opcode[6:2]), .b(5'b01000), .eq(S));  // open: gt, lt
  Comparator #(.width(5)) comparator_8 (.a(opcode[6:2]), .b(5'b11000), .eq(B));  // open: gt, lt
  Comparator #(.width(5)) comparator_9 (.a(opcode[6:2]), .b(5'b01101), .eq(comparator_9_eq));  // open: gt, lt
  Comparator #(.width(5)) comparator_10 (.a(opcode[6:2]), .b(5'b00101), .eq(comparator_10_eq));  // open: gt, lt
  Comparator #(.width(5)) comparator_11 (.a(opcode[6:2]), .b(5'b11011), .eq(J));  // open: gt, lt
  or or_2 (I, comparator_3_eq, demultiplexer_1_out0, comparator_5_eq);
  or or_3 (R, demultiplexer_1_out1, comparator_6_eq);
  or or_4 (U, comparator_9_eq, comparator_10_eq);
endmodule

module branch_evaluator (
  input  [31:0] rs1,
  input  [31:0] rs2,
  input  [2:0] funct3,
  output out_4
);

  wire comparator_1_eq, comparator_1_lt, comparator_2_gt, multiplexer_1_out, undriven;

  Comparator #(.width(32)) comparator_1 (.a(rs1), .b(rs2), .eq(comparator_1_eq), .lt(comparator_1_lt));  // open: gt
  Comparator #(.width(32), .mode("unsigned")) comparator_2 (.a(rs2), .b(rs1), .gt(comparator_2_gt));  // open: eq, lt
  Multiplexer #(.select(2)) multiplexer_1 (
    .in0(comparator_1_eq), .in1(comparator_1_lt), .in2(comparator_1_lt), .in3(comparator_2_gt),
    .out(multiplexer_1_out), .sel(funct3[2:1]), .en(undriven));
  xor xor_1 (out_4, multiplexer_1_out, funct3[0]);

  // Notes on the sheet:
  //   NOTE: 010 and 011 are invalid funct3 values for branch. they are treated as if they were 100 and 101
  //   least significant bit of funct3 inverts branch
endmodule

module LUI_AUIPC_JAL_JALR (
  input  [6:0] in_1,
  output JALR,
  output JAL,
  output AUIPC,
  output LUI,
  output Load,
  output Store
);

  Comparator #(.width(7)) comparator_1 (.a(7'b1100111), .b(in_1), .eq(JALR));  // open: gt, lt
  Comparator #(.width(7)) comparator_2 (.a(7'b1101111), .b(in_1), .eq(JAL));  // open: gt, lt
  Comparator #(.width(7)) comparator_3 (.a(7'b0010111), .b(in_1), .eq(AUIPC));  // open: gt, lt
  Comparator #(.width(7)) comparator_4 (.a(7'b0110111), .b(in_1), .eq(LUI));  // open: gt, lt
  Comparator #(.width(7)) comparator_5 (.a(7'b0000011), .b(in_1), .eq(Load));  // open: gt, lt
  Comparator #(.width(7)) comparator_6 (.a(7'b0100011), .b(in_1), .eq(Store));  // open: gt, lt
endmodule

module register_write (
  input  [6:0] in_1,
  output out_2
);

  wire comparator_1_eq, comparator_2_eq, comparator_3_eq, comparator_4_eq, comparator_5_eq, comparator_6_eq,
       comparator_7_eq;

  Comparator #(.width(7)) comparator_1 (.a(7'b0000011), .b(in_1), .eq(comparator_1_eq));  // open: gt, lt
  Comparator #(.width(7)) comparator_2 (.a(7'b1100111), .b(in_1), .eq(comparator_2_eq));  // open: gt, lt
  Comparator #(.width(7)) comparator_3 (.a(7'b1101111), .b(in_1), .eq(comparator_3_eq));  // open: gt, lt
  Comparator #(.width(7)) comparator_4 (.a(7'b0010111), .b(in_1), .eq(comparator_4_eq));  // open: gt, lt
  Comparator #(.width(7)) comparator_5 (.a(7'b0110111), .b(in_1), .eq(comparator_5_eq));  // open: gt, lt
  Comparator #(.width(7), .mode("unsigned")) comparator_6 (
    .a(7'b0010011), .b(in_1), .eq(comparator_6_eq));  // open: gt, lt
  Comparator #(.width(7), .mode("unsigned")) comparator_7 (
    .a(7'b0110011), .b(in_1), .eq(comparator_7_eq));  // open: gt, lt
  or or_1 (out_2, comparator_2_eq, comparator_3_eq, comparator_4_eq, comparator_1_eq, comparator_5_eq, comparator_6_eq, comparator_7_eq);

  // Notes on the sheet:
  //   0110111, 0010111, 1101111, 1100111, 0010011, 0110011, 0000011 all write to registers
endmodule

module data_out_slicer (
  input  [2:0] funct3,
  input  [31:0] address,
  input  [31:0] RAM_data,
  output [31:0] out_4
);

  wire not_1_out, not_2_out;
  wire [1:0] subtractor_1_out;
  wire [7:0] multiplexer_2_out;
  wire [15:0] multiplexer_1_out;
  wire [31:0] bit_extender_1_out, bit_extender_2_out, bit_extender_3_out, bit_extender_4_out,
       multiplexer_3_out, multiplexer_4_out, multiplexer_5_out;

  // Probe on address[1:0]
  Subtractor #(.width(2)) subtractor_1 (.a(2'b11), .b(address[1:0]), .out(subtractor_1_out));  // open: bin, bout
  not not_1 (not_1_out, address[0]);
  Multiplexer #(.width(16)) multiplexer_1 (
    .in0(RAM_data[31:16]), .in1(RAM_data[15:0]), .out(multiplexer_1_out), .sel(not_1_out));  // open: en
  Multiplexer #(.select(2), .width(8)) multiplexer_2 (
    .in0(RAM_data[31:24]), .in1(RAM_data[23:16]), .in2(RAM_data[15:8]), .in3(RAM_data[7:0]),
    .out(multiplexer_2_out), .sel(subtractor_1_out));  // open: en
  assign bit_extender_1_out = {{16{multiplexer_1_out[15]}}, multiplexer_1_out};  // Bit_Extender bit_extender_1
  Multiplexer #(.width(32)) multiplexer_3 (
    .in0(bit_extender_1_out), .in1(bit_extender_2_out), .out(multiplexer_3_out), .sel(funct3[2]));  // open: en
  assign bit_extender_2_out = {{16{1'b0}}, multiplexer_1_out};  // Bit_Extender bit_extender_2
  assign bit_extender_3_out = {{24{multiplexer_2_out[7]}}, multiplexer_2_out};  // Bit_Extender bit_extender_3
  Multiplexer #(.width(32)) multiplexer_4 (
    .in0(bit_extender_3_out), .in1(bit_extender_4_out), .out(multiplexer_4_out), .sel(funct3[2]));  // open: en
  assign bit_extender_4_out = {{24{1'b0}}, multiplexer_2_out};  // Bit_Extender bit_extender_4
  not not_2 (not_2_out, funct3[0]);
  Multiplexer #(.width(32)) multiplexer_5 (
    .in0(multiplexer_3_out), .in1(multiplexer_4_out), .out(multiplexer_5_out), .sel(not_2_out));  // open: en
  Multiplexer #(.width(32)) multiplexer_6 (
    .in0(multiplexer_5_out), .in1(RAM_data), .out(out_4), .sel(funct3[1]));  // open: en
endmodule

module data_in_stapler (
  input  [2:0] funct3,
  input  [31:0] address,
  input  [31:0] to_write,
  input  [31:0] current_value_at_location,
  output [31:0] combined_data
);

  wire [7:0] bit_extender_2_out, bitselector_2_out;
  wire [15:0] bit_extender_1_out, bitselector_1_out;
  wire [31:0] adder_1_out, adder_2_out, bit_extender_3_out, bit_extender_4_out, bit_extender_5_out,
       bit_extender_6_out, shifter_1_out, shifter_2_out, shifter_3_out, shifter_4_out, subtractor_1_out,
       subtractor_2_out;

  Bit_Extender #(.in_width(32)) bit_extender_1 (.in(to_write), .out(bit_extender_1_out));
  Bit_Extender #(.in_width(32), .out_width(8)) bit_extender_2 (.in(to_write), .out(bit_extender_2_out));
  assign bit_extender_3_out = {{16{1'b0}}, bitselector_1_out};  // Bit_Extender bit_extender_3
  BitSelector #(.width(32), .group(16)) bitselector_1 (
    .in(current_value_at_location), .out(bitselector_1_out), .sel(address[0]));
  assign bit_extender_4_out = {{16{1'b0}}, bit_extender_1_out};  // Bit_Extender bit_extender_4
  assign bit_extender_5_out = {{24{1'b0}}, bitselector_2_out};  // Bit_Extender bit_extender_5
  BitSelector #(.width(32), .group(8)) bitselector_2 (
    .in(current_value_at_location), .out(bitselector_2_out), .sel(address[1:0]));
  assign bit_extender_6_out = {{24{1'b0}}, bit_extender_2_out};  // Bit_Extender bit_extender_6
  Shifter #(.width(32)) shifter_1 (.in(bit_extender_3_out), .\dist ({address[0], 4'b0000}), .out(shifter_1_out));
  Shifter #(.width(32)) shifter_2 (.in(bit_extender_4_out), .\dist ({address[0], 4'b0000}), .out(shifter_2_out));
  Shifter #(.width(32)) shifter_3 (.in(bit_extender_5_out), .\dist ({address[1:0], 3'b000}), .out(shifter_3_out));
  Shifter #(.width(32)) shifter_4 (.in(bit_extender_6_out), .\dist ({address[1:0], 3'b000}), .out(shifter_4_out));
  Subtractor #(.width(32)) subtractor_1 (
    .a(current_value_at_location), .b(shifter_1_out), .out(subtractor_1_out));  // open: bin, bout
  Subtractor #(.width(32)) subtractor_2 (
    .a(current_value_at_location), .b(shifter_3_out), .out(subtractor_2_out));  // open: bin, bout
  Adder #(.width(32)) adder_1 (.a(subtractor_2_out), .b(shifter_4_out), .out(adder_1_out));  // open: cin, cout
  // Probe on adder_2_out
  Adder #(.width(32)) adder_2 (.a(subtractor_1_out), .b(shifter_2_out), .out(adder_2_out));  // open: cin, cout
  // Probe on adder_1_out
  Multiplexer #(.select(2), .width(32)) multiplexer_1 (
    .in0(adder_1_out), .in1(adder_2_out), .in2(to_write), .in3({32{1'b0}}), .out(combined_data),
    .sel(funct3[1:0]));  // open: en
endmodule
